# Fritzing sketch Photoresistor (saved by Fritzing 1.0.1rc)
breadboards: 1

parts:
  Mod1 = Raspberry Pi Pico W
  R1 = PHOTOCELL [package=photocell]
  R2 = Resistor [tolerance=±5% resistance=10k package="0805 [SMD]"]

nets:
  N1: Mod1.pin_1, Mod1.pin_3, Mod1.pin_5, Mod1.pin_18, Mod1.pin_23, Mod1.pin_24, Mod1.pin_38, Mod1.pin_42
  N2: Mod1.pin_2, Mod1.pin_4, Mod1.pin_40, R1.P$1
  N3: Mod1.pin_12, Mod1.pin_36
  N4: Mod1.pin_15, Mod1.pin_30
  N5: R1.P$2, R2.Pin_0

custom parts:
  Raspberry Pi Pico W: Raspberry Pi Pico W. Based around the RP2040 microcontroller the Pico W is a low cost microcontroller device bringing Raspberry Pi quality, cost, and easy of use to the microcontroller space. The areas marked KEEPOUT in pcb silkscreen should not have traces running through them to avoid shorts on a soldered in module!
